// Logisim project project r.circ as structural Verilog: 6 circuits, main circuit 1_bit_ALU
module _1_bit_ALU (
  input  Cin,
  input  A,
  input  Ain,
  input  B,
  input  Bin,
  input  [1:0] Aluop,
  output Result,
  output Cout
);

  wire adder_1_out, and_1_out, multiplexer_1_out, multiplexer_2_out, not_1_out, not_2_out, or_1_out;

  not not_1 (not_1_out, A);
  not not_2 (not_2_out, B);
  Multiplexer multiplexer_1 (.in0(A), .in1(not_1_out), .out(multiplexer_1_out), .sel(Ain));  // open: en
  Multiplexer multiplexer_2 (.in0(B), .in1(not_2_out), .out(multiplexer_2_out), .sel(Bin));  // open: en
  and and_1 (and_1_out, multiplexer_1_out, multiplexer_2_out);
  or or_1 (or_1_out, multiplexer_1_out, multiplexer_2_out);
  Adder #(.width(1)) adder_1 (.a(multiplexer_1_out), .b(multiplexer_2_out), .out(adder_1_out), .cin(Cin), .cout(Cout));
  Multiplexer #(.select(2)) multiplexer_3 (
    .in0(and_1_out), .in1(or_1_out), .in2(adder_1_out), .out(Result), .sel(Aluop));  // open: in3, en
endmodule

module _12_bit_ALU (
  input  CIN,
  input  [11:0] in_2,
  input  [1:0] ALUOP,
  input  AIN,
  input  BIN,
  input  [11:0] in_6,
  output [11:0] out_7,
  output Zero,
  output overflow
);

  wire n1_bit_alu_1_cout, n1_bit_alu_2_cout, n1_bit_alu_3_cout, n1_bit_alu_4_cout, n1_bit_alu_5_cout,
       n1_bit_alu_6_cout, n1_bit_alu_7_cout, n1_bit_alu_8_cout, n1_bit_alu_9_cout, n1_bit_alu_11_cout;

  _1_bit_ALU u_1_bit_alu_1 (
    .A(in_2[0]), .Ain(AIN), .B(in_6[0]), .Bin(BIN), .Result(out_7[0]), .Cout(n1_bit_alu_1_cout), .Cin(CIN),
    .Aluop(ALUOP));
  _1_bit_ALU u_1_bit_alu_2 (
    .A(in_2[1]), .Ain(AIN), .B(in_6[1]), .Bin(BIN), .Result(out_7[1]), .Cout(n1_bit_alu_2_cout),
    .Cin(n1_bit_alu_1_cout), .Aluop(ALUOP));
  _1_bit_ALU u_1_bit_alu_3 (
    .A(in_2[2]), .Ain(AIN), .B(in_6[2]), .Bin(BIN), .Result(out_7[2]), .Cout(n1_bit_alu_3_cout),
    .Cin(n1_bit_alu_2_cout), .Aluop(ALUOP));
  _1_bit_ALU u_1_bit_alu_4 (
    .A(in_2[3]), .Ain(AIN), .B(in_6[3]), .Bin(BIN), .Result(out_7[3]), .Cout(n1_bit_alu_4_cout),
    .Cin(n1_bit_alu_3_cout), .Aluop(ALUOP));
  _1_bit_ALU u_1_bit_alu_5 (
    .A(in_2[4]), .Ain(AIN), .B(in_6[4]), .Bin(BIN), .Result(out_7[4]), .Cout(n1_bit_alu_5_cout),
    .Cin(n1_bit_alu_4_cout), .Aluop(ALUOP));
  _1_bit_ALU u_1_bit_alu_6 (
    .A(in_2[5]), .Ain(AIN), .B(in_6[5]), .Bin(BIN), .Result(out_7[5]), .Cout(n1_bit_alu_6_cout),
    .Cin(n1_bit_alu_5_cout), .Aluop(ALUOP));
  _1_bit_ALU u_1_bit_alu_7 (
    .A(in_2[6]), .Ain(AIN), .B(in_6[6]), .Bin(BIN), .Result(out_7[6]), .Cout(n1_bit_alu_7_cout),
    .Cin(n1_bit_alu_6_cout), .Aluop(ALUOP));
  _1_bit_ALU u_1_bit_alu_8 (
    .A(in_2[7]), .Ain(AIN), .B(in_6[7]), .Bin(BIN), .Result(out_7[7]), .Cout(n1_bit_alu_8_cout),
    .Cin(n1_bit_alu_7_cout), .Aluop(ALUOP));
  _1_bit_ALU u_1_bit_alu_9 (
    .A(in_2[8]), .Ain(AIN), .B(in_6[8]), .Bin(BIN), .Result(out_7[8]), .Cout(n1_bit_alu_9_cout),
    .Cin(n1_bit_alu_8_cout), .Aluop(ALUOP));
  _1_bit_ALU u_1_bit_alu_10 (
    .A(in_2[9]), .Ain(AIN), .B(in_6[9]), .Bin(BIN), .Result(out_7[9]), .Cin(n1_bit_alu_9_cout), .Aluop(ALUOP));  // open: Cout
  _1_bit_ALU u_1_bit_alu_11 (
    .A(in_2[10]), .Ain(AIN), .B(in_6[10]), .Bin(BIN), .Result(out_7[10]), .Cout(n1_bit_alu_11_cout),
    .Aluop(ALUOP));  // open: Cin
  _1_bit_ALU u_1_bit_alu_12 (
    .A(in_2[11]), .Ain(AIN), .B(in_6[11]), .Bin(BIN), .Result(out_7[11]), .Cout(overflow),
    .Cin(n1_bit_alu_11_cout), .Aluop(ALUOP));
  nor nor_1 (Zero, out_7[0], out_7[1], out_7[2], out_7[3], out_7[4], out_7[5], out_7[6], out_7[7], out_7[8], out_7[9], out_7[10], out_7[11]);

  // Notes on the sheet:
  //   A
  //   B
  //   RESULT
endmodule

module reg_file (
  input  [11:0] in_1,
  input  in_2,
  input  [2:0] RS,
  input  [2:0] in_4,
  input  in_5,
  input  [2:0] RT,
  output [11:0] out_7,
  output [11:0] out_8
);

  wire demultiplexer_1_out0, demultiplexer_1_out1, demultiplexer_1_out2, demultiplexer_1_out3,
       demultiplexer_1_out4, demultiplexer_1_out5, demultiplexer_1_out6, demultiplexer_1_out7;
  wire [11:0] register_1_q, register_2_q, register_3_q, register_4_q, register_5_q, register_6_q,
       register_7_q, register_8_q;

  Demultiplexer #(.select(3)) demultiplexer_1 (
    .out0(demultiplexer_1_out0), .out1(demultiplexer_1_out1), .out2(demultiplexer_1_out2),
    .out3(demultiplexer_1_out3), .out4(demultiplexer_1_out4), .out5(demultiplexer_1_out5),
    .out6(demultiplexer_1_out6), .out7(demultiplexer_1_out7), .in(in_2), .sel(in_4));  // open: en
  Register #(.width(12)) register_1 (.D(in_1), .en(demultiplexer_1_out0), .Q(register_1_q), .clk(in_5));  // open: clr
  Register #(.width(12)) register_2 (.D(in_1), .en(demultiplexer_1_out1), .Q(register_2_q), .clk(in_5));  // open: clr
  Register #(.width(12)) register_3 (.D(in_1), .en(demultiplexer_1_out2), .Q(register_3_q), .clk(in_5));  // open: clr
  Register #(.width(12)) register_4 (.D(in_1), .en(demultiplexer_1_out3), .Q(register_4_q), .clk(in_5));  // open: clr
  Register #(.width(12)) register_5 (.D(in_1), .en(demultiplexer_1_out4), .Q(register_5_q), .clk(in_5));  // open: clr
  Register #(.width(12)) register_6 (.D(in_1), .en(demultiplexer_1_out5), .Q(register_6_q), .clk(in_5));  // open: clr
  Register #(.width(12)) register_7 (.D(in_1), .en(demultiplexer_1_out6), .Q(register_7_q), .clk(in_5));  // open: clr
  Register #(.width(12)) register_8 (.D(in_1), .en(demultiplexer_1_out7), .Q(register_8_q), .clk(in_5));  // open: clr
  Multiplexer #(.select(3), .width(12)) multiplexer_1 (
    .in0(register_1_q), .in1(register_2_q), .in2(register_3_q), .in3(register_4_q), .in4(register_5_q),
    .in5(register_6_q), .in6(register_7_q), .in7(register_8_q), .out(out_7), .sel(RS));  // open: en
  Multiplexer #(.select(3), .width(12)) multiplexer_2 (
    .in0(register_1_q), .in1(register_2_q), .in2(register_3_q), .in3(register_4_q), .in4(register_5_q),
    .in5(register_6_q), .in6(register_7_q), .in7(register_8_q), .out(out_8), .sel(RT));  // open: en

  // Notes on the sheet:
  //   R0
  //   R1
  //   R2
  //   R3
  //   R4
  //   R5
  //   R6
  //   R7
endmodule

module Full_single_cycle_datapath (
  input  [11:0] in_1,
  input  in_2,
  input  Reg_Dst,
  input  Write_enb,
  input  [1:0] ALU_OP,
  input  ALU_Src,
  input  Sub,
  input  Store_enb,
  input  Load_enb,
  input  RAM_Reg,
  input  Jump,
  output [11:0] Jump_addr,
  output [2:0] Opcode,
  output [11:0] data_1,
  output [11:0] out_15,
  output [2:0] Rs_read_reg_1,
  output [2:0] Rt_read_reg_2,
  output [11:0] data_2,
  output [2:0] Rd_write_reg,
  output [11:0] result_val,
  output zero,
  output out_22,
  output [11:0] Data_for_store
);

  wire clock_out;
  wire [2:0] multiplexer_2_out;
  wire [11:0] bit_extender_1_out, multiplexer_1_out, n12_bit_alu_1_out_7, PC_q, ram_1_data;

  Multiplexer #(.width(12), .enable("false")) multiplexer_1 (
    .in0({Jump_addr[11:9], out_15[8:0]}), .in1(Jump_addr), .out(multiplexer_1_out), .sel(Jump));
  Register #(.width(12)) PC (.D(multiplexer_1_out), .Q(PC_q), .clk(clock_out));  // open: en, clr
  Clock clock (.out(clock_out));
  Adder #(.width(12)) adder_1 (.a(PC_q), .b(in_1), .out({Jump_addr[11:9], out_15[8:0]}));  // open: cin, cout
  ROM #(.addrWidth(12), .dataWidth(12)) rom_1 (.addr(PC_q), .data({Opcode, Jump_addr[8:0]}));  // open: sel
  Multiplexer #(.width(3), .enable("false")) multiplexer_2 (
    .in0(Jump_addr[2:0]), .in1(Jump_addr[5:3]), .out(multiplexer_2_out), .sel(Reg_Dst));
  reg_file reg_file_1 (
    .in_1(result_val), .out_7(data_1), .in_2(Write_enb), .RS(Jump_addr[8:6]), .in_4(multiplexer_2_out),
    .in_5(clock_out), .out_8(Data_for_store), .RT(Jump_addr[5:3]));
  assign bit_extender_1_out = {{9{1'b0}}, Jump_addr[2:0]};  // Bit_Extender bit_extender_1
  Multiplexer #(.width(12), .enable("false")) multiplexer_3 (
    .in0(Data_for_store), .in1(bit_extender_1_out), .out(data_2), .sel(ALU_Src));
  _12_bit_ALU u_12_bit_alu_1 (
    .CIN(Sub), .in_2(data_1), .out_7(n12_bit_alu_1_out_7), .ALUOP(ALU_OP), .AIN(in_2), .BIN(Sub),
    .in_6(data_2), .Zero(zero), .overflow(out_22));
  RAM #(.addrWidth(12), .dataWidth(12), .bus("separate")) ram_1 (
    .addr(n12_bit_alu_1_out_7), .din(Data_for_store), .data(ram_1_data), .str(Store_enb), .clk(clock_out),
    .ld(Load_enb));  // open: sel, clr
  Multiplexer #(.width(12), .enable("false")) multiplexer_4 (
    .in0(n12_bit_alu_1_out_7), .in1(ram_1_data), .out(result_val), .sel(RAM_Reg));

  assign out_15[11:9] = Jump_addr[11:9];
  assign Rd_write_reg = Jump_addr[2:0];
  assign Rs_read_reg_1 = Jump_addr[8:6];
  assign Rt_read_reg_2 = Jump_addr[5:3];

  // Notes on the sheet:
  //   contents of rom_1 (hex, n*v repeats v):
  //   123
endmodule

module single_cycle_with_CU (
  input  [11:0] in_1,
  input  in_2,
  output [11:0] Jump_addr,
  output [2:0] Opcode,
  output [11:0] data_1,
  output [11:0] out_6,
  output [2:0] Rs_read_reg_1,
  output [2:0] Rt_read_reg_2,
  output [11:0] data_2,
  output [2:0] Rd_write_reg,
  output [11:0] result_val,
  output zero,
  output out_13,
  output [11:0] Data_for_store
);

  wire clock_out, contro_unit_1_alu_src, contro_unit_1_jump, contro_unit_1_load_enb,
       contro_unit_1_ram_to_reg, contro_unit_1_reg_dst, contro_unit_1_store_enb, contro_unit_1_sub,
       contro_unit_1_write_enb;
  wire [1:0] contro_unit_1_alu_op;
  wire [2:0] multiplexer_2_out;
  wire [11:0] bit_extender_1_out, multiplexer_1_out, n12_bit_alu_1_out_7, PC_q, ram_1_data;

  Multiplexer #(.width(12), .enable("false")) multiplexer_1 (
    .in0({Jump_addr[11:9], out_6[8:0]}), .in1(Jump_addr), .out(multiplexer_1_out), .sel(contro_unit_1_jump));
  Register #(.width(12)) PC (.D(multiplexer_1_out), .Q(PC_q), .clk(clock_out));  // open: en, clr
  Clock clock (.out(clock_out));
  Contro_unit contro_unit_1 (
    .Reg_dst(contro_unit_1_reg_dst), .Write_enb(contro_unit_1_write_enb), .alu_src(contro_unit_1_alu_src),
    .sub(contro_unit_1_sub), .store_enb(contro_unit_1_store_enb), .load_enb(contro_unit_1_load_enb),
    .ram_to_reg(contro_unit_1_ram_to_reg), .jump(contro_unit_1_jump), .ALU_OP(contro_unit_1_alu_op),
    .in_1(Opcode));
  Adder #(.width(12)) adder_1 (.a(PC_q), .b(in_1), .out({Jump_addr[11:9], out_6[8:0]}));  // open: cin, cout
  ROM #(.addrWidth(12), .dataWidth(12)) rom_1 (.addr(PC_q), .data({Opcode, Jump_addr[8:0]}));  // open: sel
  Multiplexer #(.width(3), .enable("false")) multiplexer_2 (
    .in0(Jump_addr[2:0]), .in1(Jump_addr[5:3]), .out(multiplexer_2_out), .sel(contro_unit_1_reg_dst));
  reg_file reg_file_1 (
    .in_1(result_val), .out_7(data_1), .in_2(contro_unit_1_write_enb), .RS(Jump_addr[8:6]),
    .in_4(multiplexer_2_out), .in_5(clock_out), .out_8(Data_for_store), .RT(Jump_addr[5:3]));
  assign bit_extender_1_out = {{9{1'b0}}, Jump_addr[2:0]};  // Bit_Extender bit_extender_1
  Multiplexer #(.width(12), .enable("false")) multiplexer_3 (
    .in0(Data_for_store), .in1(bit_extender_1_out), .out(data_2), .sel(contro_unit_1_alu_src));
  _12_bit_ALU u_12_bit_alu_1 (
    .CIN(contro_unit_1_sub), .in_2(data_1), .out_7(n12_bit_alu_1_out_7), .ALUOP(contro_unit_1_alu_op),
    .AIN(in_2), .BIN(contro_unit_1_sub), .in_6(data_2), .Zero(zero), .overflow(out_13));
  RAM #(.addrWidth(12), .dataWidth(12), .bus("separate")) ram_1 (
    .addr(n12_bit_alu_1_out_7), .din(Data_for_store), .data(ram_1_data), .str(contro_unit_1_store_enb),
    .clk(clock_out), .ld(contro_unit_1_load_enb));  // open: sel, clr
  Multiplexer #(.width(12), .enable("false")) multiplexer_4 (
    .in0(n12_bit_alu_1_out_7), .in1(ram_1_data), .out(result_val), .sel(contro_unit_1_ram_to_reg));

  assign out_6[11:9] = Jump_addr[11:9];
  assign Rd_write_reg = Jump_addr[2:0];
  assign Rs_read_reg_1 = Jump_addr[8:6];
  assign Rt_read_reg_2 = Jump_addr[5:3];

  // Notes on the sheet:
  //   contents of rom_1 (hex, n*v repeats v):
  //   c08
endmodule

module Contro_unit (
  input  [2:0] in_1,
  output Reg_dst,
  output Write_enb,
  output [1:0] ALU_OP,
  output alu_src,
  output sub,
  output store_enb,
  output load_enb,
  output ram_to_reg,
  output jump
);

  wire and_3_out, and_4_out, and_5_out, and_6_out, and_7_out, and_8_out, and_9_out, and_10_out, and_12_out,
       and_13_out, not_1_out, not_2_out, not_3_out, not_4_out, not_5_out, not_6_out, not_7_out, not_8_out,
       not_9_out, not_10_out, not_11_out, not_12_out, not_13_out, not_14_out, not_15_out, not_16_out,
       not_17_out, not_18_out;

  not not_1 (not_1_out, in_1[2]);
  not not_2 (not_2_out, in_1[2]);
  not not_3 (not_3_out, in_1[1]);
  not not_4 (not_4_out, in_1[2]);
  not not_5 (not_5_out, in_1[0]);
  not not_6 (not_6_out, in_1[1]);
  not not_7 (not_7_out, in_1[0]);
  not not_8 (not_8_out, in_1[2]);
  not not_9 (not_9_out, in_1[0]);
  not not_10 (not_10_out, in_1[2]);
  not not_11 (not_11_out, in_1[2]);
  not not_12 (not_12_out, in_1[0]);
  not not_13 (not_13_out, in_1[2]);
  not not_14 (not_14_out, in_1[1]);
  not not_15 (not_15_out, in_1[0]);
  not not_16 (not_16_out, in_1[1]);
  and and_1 (load_enb, in_1[2], in_1[1], in_1[0]);
  and and_2 (ram_to_reg, in_1[2], in_1[1], in_1[0]);
  not not_17 (not_17_out, in_1[0]);
  and and_3 (and_3_out, not_1_out, in_1[1]);
  and and_4 (and_4_out, in_1[2], in_1[0]);
  and and_5 (and_5_out, not_2_out, not_3_out);
  and and_6 (and_6_out, not_4_out, not_5_out);
  and and_7 (and_7_out, not_6_out, not_7_out);
  and and_8 (and_8_out, in_1[2], in_1[1], in_1[0]);
  and and_9 (and_9_out, not_8_out, not_9_out);
  not not_18 (not_18_out, in_1[1]);
  and and_10 (and_10_out, in_1[2], in_1[0]);
  and and_11 (ALU_OP[0], not_10_out, in_1[1], in_1[0]);
  and and_12 (and_12_out, not_11_out, in_1[1], not_12_out);
  and and_13 (and_13_out, in_1[2], in_1[0]);
  and and_14 (sub, not_13_out, not_14_out, not_15_out);
  and and_15 (store_enb, in_1[2], not_16_out, in_1[0]);
  and and_16 (jump, in_1[2], in_1[1], not_17_out);
  or or_1 (Reg_dst, and_3_out, and_4_out);
  or or_2 (Write_enb, and_5_out, and_6_out, and_7_out, and_8_out);
  or or_3 (ALU_OP[1], and_9_out, not_18_out, and_10_out);
  or or_4 (alu_src, and_12_out, and_13_out);
endmodule
